// Logisim project Instructions.circ as structural Verilog: 1 circuit, main circuit main
module main (
  input  in_1,
  input  in_2,
  input  in_3,
  input  in_4,
  input  in_5
);

  wire AC_ON, and_2_out, AR_ON, CLK, D0T4, D0T5, decoder_1_out0, decoder_1_out1, decoder_1_out2,
       decoder_1_out3, decoder_2_out0, decoder_2_out7, or_1_out, RAM_LOAD_ON, register_1_q, T4, T5;
  wire [2:0] counter_6_q, or_6_out;
  wire [11:0] bit_extender_1_out, bit_extender_2_out, counter_1_q, counter_2_q;
  wire [15:0] and_1_out, bit_extender_3_out, bit_extender_4_out, counter_4_q, counter_5_q, DECODE_INS,
       multiplexer_1_out, ram_1_data;

  Clock clock_1 (.out(CLK));
  Counter #(.width(12), .max('hfff)) counter_1 (
    .load(AR_ON), .D(bit_extender_1_out), .count(in_3), .Q(counter_1_q), .clk(CLK), .clr(in_3));  // open: carry
  Bit_Extender #(.in_width(16), .out_width(12)) bit_extender_1 (.in(multiplexer_1_out), .out(bit_extender_1_out));
  Bit_Extender #(.in_width(16), .out_width(12)) bit_extender_2 (.in(multiplexer_1_out), .out(bit_extender_2_out));
  Counter #(.width(12), .max('hfff)) counter_2 (
    .D(bit_extender_2_out), .count(or_1_out), .Q(counter_2_q), .clk(CLK));  // open: load, carry, clr
  Counter #(.width(16), .max('hffff)) counter_3 (
    .load(or_1_out), .D(multiplexer_1_out), .count(in_3), .Q(DECODE_INS), .clk(CLK));  // open: carry, clr
  Counter #(.width(16), .max('hffff)) counter_4 (
    .load(AC_ON), .D(and_1_out), .count(in_1), .Q(counter_4_q), .clk(CLK));  // open: carry, clr
  Counter #(.width(16), .max('hffff)) counter_5 (
    .load(D0T4), .D(multiplexer_1_out), .count(in_1), .Q(counter_5_q), .clk(CLK));  // open: carry, clr
  assign bit_extender_3_out = {{4{1'b0}}, counter_1_q};  // Bit_Extender bit_extender_3
  assign bit_extender_4_out = {{4{1'b0}}, counter_2_q};  // Bit_Extender bit_extender_4
  buf or_1 (or_1_out, decoder_1_out1);  // OR_Gate
  RAM #(.addrWidth(12), .dataWidth(16), .bus("separate")) ram_1 (
    .addr(counter_1_q), .data(ram_1_data), .str(in_5), .clk(CLK), .ld(RAM_LOAD_ON));  // open: din, sel, clr
  or or_2 (AR_ON, decoder_1_out0, and_2_out, decoder_1_out2);
  Counter #(.width(3), .max('h7)) counter_6 (.Q(counter_6_q), .clk(CLK));  // open: load, D, count, carry, clr
  Decoder #(.select(3), .enable("false")) decoder_1 (
    .out0(decoder_1_out0), .out1(decoder_1_out1), .out2(decoder_1_out2), .out3(decoder_1_out3), .out4(T4),
    .out5(T5), .sel(counter_6_q));  // open: out6, out7
  assign and_1_out = counter_4_q & counter_5_q;  // AND_Gate and_1, 16 bits wide
  Multiplexer #(.select(3), .width(16), .enable("false")) multiplexer_1 (
    .in1(bit_extender_3_out), .in2(bit_extender_4_out), .in3(counter_5_q), .in5(DECODE_INS),
    .in7(ram_1_data), .out(multiplexer_1_out), .sel(or_6_out));  // open: in0, in4, in6
  or or_3 (RAM_LOAD_ON, decoder_1_out1, D0T4, decoder_1_out3);
  Register #(.width(1)) register_1 (.D(DECODE_INS[15]), .Q(register_1_q), .clk(CLK));  // open: en, clr
  Decoder #(.select(3), .enable("false")) decoder_2 (
    .out0(decoder_2_out0), .out7(decoder_2_out7), .sel(DECODE_INS[14:12]));  // open: out1, out2, out3, out4, out5, out6
  or or_4 (or_6_out[2], decoder_1_out3, decoder_1_out1, decoder_1_out2, D0T4);
  or or_5 (or_6_out[1], decoder_1_out0, decoder_1_out1, decoder_1_out3, D0T4);
  or or_6 (or_6_out[0], decoder_1_out3, decoder_1_out1, decoder_1_out2, D0T4);
  and and_2 (and_2_out, ~decoder_2_out7, register_1_q, decoder_1_out3);  // AND_Gate
  and and_3 (D0T4, decoder_2_out0, T4);
  and and_4 (D0T5, decoder_2_out0, T5);
  buf or_7 (AC_ON, D0T5);  // OR_Gate

  // Other names for the same wires on the sheet: DR_ON = D0T4; RAM_STORE_ON = in_5

  // Notes on the sheet:
  //   AR
  //   AC
  //   DR
  //   PC
  //   IR
  //   Indirect Bit
endmodule
